# Fritzing sketch smart_citizen_board_arduino_pro_mini_5v_jst (saved by Fritzing 0.9.2b)
circuit board: 6.5cm x 3.19575cm
breadboards: 1

parts:
  D1 = Rectifier Diode [part_number=1N4001 package="300 mil [THT]"]
  R1 = Resistor [tolerance=±5% resistance=100k package=THT]
  PWR = female pin header, 2 pins [form="♀ (female)"]
  D2 = Rectifier Diode [part_number=1N4001 package="300 mil [THT]"]
  U2 = ESP8266 WiFi Module [part_number=ESP8266]
  CD4048B2 = CD4048B [part_number=CD4050 package="DIP (Dual Inline) [THT]"]
  Arduino_Pro_Mini = Arduino Pro Mini v13
  3_3V_SELECTOR = male pin header, 3 pins [form="♂ (male)"]
  IN-0 = Header 3 [package=molex-1x3_lock]
  IN-2 = Header 3 [package=molex-1x3_lock]
  IN-3 = Header 3 [package=molex-1x3_lock]
  IN-1 = Header 3 [package=molex-1x3_lock]
  DIGITAL_PINS = female pin header, 7 pins [form="♀ (female)"]
  5V = female pin header, 7 pins [form="♀ (female)"]
  GND = female pin header, 7 pins [form="♀ (female)"]
  3_3V = female pin header, 7 pins [form="♀ (female)"]

nets:
  N1: D1.cathode, D2.anode, 3_3V_SELECTOR.pin1
  N2: D1.anode, PWR.pin2, Arduino_Pro_Mini.VCC, IN-0.3, IN-2.3, IN-3.3, IN-1.3, 5V.pin1, 5V.pin7
  N3: R1.Pin_0, D2.cathode, 3_3V_SELECTOR.pin3
  GND: R1.Pin_1, PWR.pin1, U2.GND, CD4048B2.VSS, Arduino_Pro_Mini.GND, IN-0.1, IN-2.1, IN-3.1, IN-1.1, GND.pin1, GND.pin7
  N4: U2.RXD, CD4048B2.EXPAND
  N5: U2.VCC, U2.GPIO_0, U2.GPIO_2, CD4048B2.J, 3_3V_SELECTOR.pin2
  N6: U2.RST, CD4048B2.C
  N7: U2.CH_PD, CD4048B2.Ka
  N8: U2.TXD, Arduino_Pro_Mini.D9_PWM
  N9: CD4048B2.Kc, Arduino_Pro_Mini.D10_PWM/SS
  N10: CD4048B2.D, Arduino_Pro_Mini.D11_PWM/MOSI
  N11: CD4048B2.A, Arduino_Pro_Mini.D12/MISO
  N12: Arduino_Pro_Mini.A3, IN-3.2
  N13: Arduino_Pro_Mini.A2, IN-2.2
  N14: Arduino_Pro_Mini.A1, IN-1.2
  N15: Arduino_Pro_Mini.A0, IN-0.2
  N16: Arduino_Pro_Mini.D8, DIGITAL_PINS.pin7
  N17: Arduino_Pro_Mini.D7, DIGITAL_PINS.pin6
  N18: Arduino_Pro_Mini.D6_PWM, DIGITAL_PINS.pin5
  N19: Arduino_Pro_Mini.D5_PWM, DIGITAL_PINS.pin4
  N20: Arduino_Pro_Mini.D4, DIGITAL_PINS.pin3
  N21: Arduino_Pro_Mini.D3_PWM, DIGITAL_PINS.pin2
  N22: Arduino_Pro_Mini.D2, DIGITAL_PINS.pin1
  N23: 3_3V.pin1, 3_3V.pin7

notes:
  Alex Porto
  +
  -
  CC-by-SA

custom parts:
  ESP8266 WiFi Module: Generic WiFi Module based on the ESP8266 with onboard PCB antenna and UART communications
