# Fritzing sketch smart_citizen_board_arduino_uno_jst (saved by Fritzing 0.9.2b)
circuit board: 6.88566cm x 5.36311cm
breadboards: 1

parts:
  D1 = Rectifier Diode [part_number=1N4001 package="300 mil [THT]"]
  R1 = Resistor [tolerance=±5% resistance=100k package=THT]
  PWR = female pin header, 2 pins [form="♀ (female)"]
  D2 = Rectifier Diode [part_number=1N4001 package="300 mil [THT]"]
  U2 = ESP8266 WiFi Module [part_number=ESP8266]
  CD4048B2 = CD4048B [part_number=CD4050 package="DIP (Dual Inline) [THT]"]
  3_3V = male pin header, 3 pins [form="♂ (male)"]
  J5 = female pin header, 8 pins [form="♀ (female)"]
  GND = female pin header, 8 pins [form="♀ (female)"]
  J3 = female pin header, 7 pins [form="♀ (female)"]
  Arduino_Pro_Mini = Arduino Uno (Rev3)
  J-A0 = Header 3 [package=molex-1x3_lock]
  J-A1 = Header 3 [package=molex-1x3_lock]
  J-A2 = Header 3 [package=molex-1x3_lock]
  J-A3 = Header 3 [package=molex-1x3_lock]
  J-A4 = Header 3 [package=molex-1x3_lock]
  J-A5 = Header 3 [package=molex-1x3_lock]

nets:
  N1: D1.cathode, D2.anode, 3_3V.pin1
  N2: D1.anode, PWR.pin2, J5.pin1, J5.pin2, J5.pin3, J5.pin4, J5.pin5, J5.pin6, J5.pin7, J5.pin8, Arduino_Pro_Mini.5V, J-A0.1, J-A1.1, J-A2.1, J-A3.1, J-A4.1, J-A5.1
  N3: R1.Pin_0, D2.cathode, 3_3V.pin3
  GND: R1.Pin_1, PWR.pin1, U2.GND, CD4048B2.VSS, GND.pin1, GND.pin2, GND.pin3, GND.pin4, GND.pin5, GND.pin6, GND.pin7, GND.pin8, Arduino_Pro_Mini.GND, J-A0.3, J-A1.3, J-A2.3, J-A3.3, J-A4.3, J-A5.3
  N4: U2.RXD, CD4048B2.EXPAND
  N5: U2.VCC, U2.GPIO_0, U2.GPIO_2, CD4048B2.J, 3_3V.pin2
  N6: U2.RST, CD4048B2.C
  N7: U2.CH_PD, CD4048B2.Ka
  N8: U2.TXD, Arduino_Pro_Mini.D9_PWM
  N9: CD4048B2.Kc, Arduino_Pro_Mini.D10_PWM/SS
  N10: CD4048B2.D, Arduino_Pro_Mini.D11_PWM/MOSI
  N11: CD4048B2.A, Arduino_Pro_Mini.D12/MISO
  N12: J3.pin1, Arduino_Pro_Mini.D2
  N13: J3.pin2, Arduino_Pro_Mini.D3_PWM
  N14: J3.pin3, Arduino_Pro_Mini.D4
  N15: J3.pin4, Arduino_Pro_Mini.D5_PWM
  N16: J3.pin5, Arduino_Pro_Mini.D6_PWM
  N17: J3.pin6, Arduino_Pro_Mini.D7
  N18: J3.pin7, Arduino_Pro_Mini.D8
  N19: Arduino_Pro_Mini.A0, J-A0.2
  N20: Arduino_Pro_Mini.A1, J-A1.2
  N21: Arduino_Pro_Mini.A2, J-A2.2
  N22: Arduino_Pro_Mini.A3, J-A3.2
  N23: Arduino_Pro_Mini.A4/SDA, J-A4.2
  N24: Arduino_Pro_Mini.A5/SCL, J-A5.2

notes:
  Alex
  CC-by-SA
  Porto
  DISC

custom parts:
  ESP8266 WiFi Module: Generic WiFi Module based on the ESP8266 with onboard PCB antenna and UART communications
