# Fritzing sketch arduino_esp2866_adapter (saved by Fritzing 0.9.2b)
circuit board: 1.8cm x 5.3cm
breadboards: 1

parts:
  CD4048B2 = CD4048B [part_number=CD4050 package="DIP (Dual Inline) [THT]"]
  D2 = Rectifier Diode [part_number=1N4001 package="300 mil [THT]"]
  R1 = Resistor [tolerance=±5% resistance=100k package=THT]
  3_3V = male pin header, 3 pins [form="♂ (male)"]
  J2 = female pin header, 2 pins [form="♀ (female)"]
  D3 = Rectifier Diode [part_number=1N4001 package="300 mil [THT]"]
  U2 = ESP8266 WiFi Module [part_number=ESP8266]
  J3 = female pin header, 2 pins [form="♀ (female)"]
  J1 = female pin header, 4 pins [form="♀ (female)"]
  Pad1 = Pad [width=1 height=1 connect=center]

nets:
  N1: CD4048B2.J, 3_3V.pin2, U2.VCC, U2.GPIO_0, U2.GPIO_2, Pad1.pad
  N2: CD4048B2.Kd, U2.CH_PD
  N3: CD4048B2.H, J1.pin1
  N4: CD4048B2.G, U2.RST
  N5: CD4048B2.F, J1.pin2
  N6: CD4048B2.E, U2.RXD
  N7: CD4048B2.Kb, J1.pin3
  GND: CD4048B2.VSS, R1.Pin_1, J2.pin1, U2.GND, J3.pin1
  N8: D2.cathode, 3_3V.pin1, D3.anode
  N9: D2.anode, J2.pin2, J3.pin2
  N10: R1.Pin_0, 3_3V.pin3, D3.cathode
  N11: U2.TXD, J1.pin4

notes:
  Alex Porto

custom parts:
  ESP8266 WiFi Module: Generic WiFi Module based on the ESP8266 with onboard PCB antenna and UART communications
