# Fritzing sketch esp8266_test (saved by Fritzing 0.9.2b)
breadboards: 1

parts:
  Part1 = Arduino Mega 2560 (Rev3)
  R1 = Resistor [tolerance=±5% resistance=220 package="0402 [SMD]"]
  VCC1 = 4 x AAA Battery Mount
  D1 = Rectifier Diode [part_number=1N4001 package="300 mil [THT]"]
  CD4048B1 = CD4048B [part_number=CD4050 package="DIP (Dual Inline) [THT]"]
  U1 = ESP8266 WiFi Module [part_number=ESP8266]

nets:
  N1: Part1.D19/RX1, U1.TXD
  N2: Part1.D18/TX1, CD4048B1.H
  GND: Part1.GND, R1.Pin_1, VCC1.-, CD4048B1.VSS, U1.GND
  N3: R1.Pin_0, D1.cathode, CD4048B1.J, CD4048B1.Kd, U1.RXD, U1.VCC, U1.GPIO_0, U1.RST, U1.GPIO_2, U1.CH_PD
  N4: VCC1.+, D1.anode

custom parts:
  ESP8266 WiFi Module: Generic WiFi Module based on the ESP8266 with onboard PCB antenna and UART communications
