# Fritzing sketch treadmill_arduino_uno (saved by Fritzing 0.9.3b)
circuit board: 8.5cm x 5.3cm
breadboards: 1

parts:
  R1 = Resistor [tolerance=±5% resistance=220 package=THT]
  LCD1 = LCD screen
  Part1 = Arduino Uno (Rev3)
  R3 = TRIMPOT [package=3386u]
  J1 = female pin header, 2 pins [form="♀ (female)"]
  J2 = female pin header, 3 pins [form="♀ (female)"]
  J3 = female pin header, 4 pins [form="♀ (female)"]
  J4 = female pin header, 4 pins [form="♀ (female)"]

nets:
  VDD: R1.Pin_0, LCD1.VDD, Part1.5V, R3.CCW, J2.pin1, J3.pin1, J3.pin2, J3.pin3, J3.pin4
  N1: R1.Pin_1, LCD1.LED+
  VSS: LCD1.VSS, LCD1.R/W, LCD1.LED-, Part1.GND, R3.CW, J2.pin3, J4.pin1, J4.pin2, J4.pin3, J4.pin4
  N2: LCD1.V0, R3.WIPER
  N3: LCD1.RS, Part1.D9_PWM
  N4: LCD1.E, Part1.D6_PWM
  N5: LCD1.DB4, Part1.D2
  N6: LCD1.DB5, Part1.D3_PWM
  N7: LCD1.DB6, Part1.D4
  N8: LCD1.DB7, Part1.D5_PWM
  N9: Part1.A0, J2.pin2
  N10: Part1.D12/MISO, J1.pin1
  N11: Part1.D13/SCK, J1.pin2
